// Logisim project MIPS_MultiCycle.circ as structural Verilog: 10 circuits, main circuit main
module main (
);

  wire ALUSrcA, and_1_out, CauseWrite, clock_1_out, clock_2_out, clock_3_out, clock_4_out, clock_5_out,
       clock_6_out, clock_7_out, clock_8_out, EPCWrite, IntCause, IorD, IRWrite, MemRead, MemtoReg, MemWrite,
       or_1_out, Overflow, PCWrite, PCWriteCond, RegDst, RegWrite, Zero;
  wire [1:0] alucontrol_1_alufunct, ALUOp, ALUSrcB, PCSource;
  wire [4:0] Instruction20_16, multiplexer_2_out;
  wire [5:0] Instruction5_0, Instruction31_26;
  wire [15:6] Instruction15_0;
  wire [25:21] Instruction25_0;
  wire [31:0] A_q, ALUOut, ALUOutR, memory_1_memdata, MemoryDataReg, MemWriteData, multiplexer_1_out,
       multiplexer_3_out, multiplexer_4_out, multiplexer_5_out, multiplexer_6_out, multiplexer_7_out, PC,
       RegFile_readdata1, RegFile_readdata2, shiftl2_32bit_1_outshift32, signextend_1_out32;
  wire [31:4] shiftleft26bitto28_1_out28;

  ShiftLeft26BitTo28 shiftleft26bitto28_1 (
    .In26({Instruction25_0, Instruction20_16, Instruction15_0, Instruction5_0}),
    .Out28(shiftleft26bitto28_1_out28));
  Multiplexer #(.enable("false"), .select(2), .width(32)) multiplexer_1 (
    .in0(ALUOut), .in1(ALUOutR), .in2({shiftleft26bitto28_1_out28, PC[31:28]}), .in3(32'h80000180),
    .out(multiplexer_1_out), .sel(PCSource));
  or or_1 (or_1_out, and_1_out, PCWrite);
  Multiplexer #(.enable("false"), .width(5)) multiplexer_2 (
    .in0(Instruction20_16), .in1(Instruction15_0[15:11]), .out(multiplexer_2_out), .sel(RegDst));
  Multiplexer #(.enable("false"), .width(32)) multiplexer_3 (
    .in0(ALUOut), .in1(MemoryDataReg), .out(multiplexer_3_out), .sel(MemtoReg));
  and and_1 (and_1_out, Zero, PCWriteCond);
  Register #(.width(32)) u_PC (.D(multiplexer_1_out), .en(or_1_out), .clk(clock_1_out), .Q(PC));  // open: clr
  Clock clock_1 (.out(clock_1_out));
  SignExtend signextend_1 (.In16({Instruction15_0, Instruction5_0}), .Out32(signextend_1_out32));
  RegisterFile RegFile (
    .WriteEnable(RegWrite), .WriteRegister(multiplexer_2_out), .WriteData(multiplexer_3_out),
    .ReadRegister1(Instruction25_0), .ReadRegister2(Instruction20_16), .ReadData1(RegFile_readdata1),
    .ReadData2(RegFile_readdata2));
  Multiplexer #(.enable("false"), .width(32)) multiplexer_4 (
    .in0(PC), .in1(ALUOutR), .out(multiplexer_4_out), .sel(IorD));
  Register #(.width(32)) A (.D(RegFile_readdata1), .en(1'b1), .clk(clock_2_out), .Q(A_q));  // open: clr
  Clock clock_2 (.out(clock_2_out));
  Register #(.width(32)) B (.D(RegFile_readdata2), .en(1'b1), .clk(clock_3_out), .Q(MemWriteData));  // open: clr
  Clock clock_3 (.out(clock_3_out));
  ControlUnit1 controlunit1_1 (
    .Op(Instruction31_26), .Overflow(Overflow), .PCWriteCond(PCWriteCond), .PCWrite(PCWrite), .IorD(IorD),
    .MemRead(MemRead), .MemWrite(MemWrite), .MemtoReg(MemtoReg), .IRWrite(IRWrite), .CauseWrite(CauseWrite),
    .IntCause(IntCause), .EPCWrite(EPCWrite), .PCSource(PCSource), .ALUOp(ALUOp), .ALUSrcA(ALUSrcA),
    .ALUSrcB(ALUSrcB), .RegWrite(RegWrite), .RegDst(RegDst));
  ShiftL2_32bit shiftl2_32bit_1 (.In32(signextend_1_out32), .OutShift32(shiftl2_32bit_1_outshift32));
  Memory memory_1 (
    .MemAddr(multiplexer_4_out), .MemWrite(MemWrite), .MemRead(MemRead), .MemWriteData(MemWriteData),
    .MemData(memory_1_memdata));
  Clock clock_4 (.out(clock_4_out));
  Register #(.width(32)) MemoryDataRegister (
    .D(memory_1_memdata), .en(1'b1), .clk(clock_4_out), .Q(MemoryDataReg));  // open: clr
  Register #(.width(32)) InstructionRegister (
    .D(memory_1_memdata), .en(IRWrite), .clk(clock_5_out),
    .Q({Instruction31_26, Instruction25_0, Instruction20_16, Instruction15_0, Instruction5_0}));  // open: clr
  Clock clock_5 (.out(clock_5_out));
  Multiplexer #(.enable("false"), .width(32)) multiplexer_5 (
    .in0(PC), .in1(A_q), .out(multiplexer_5_out), .sel(ALUSrcA));
  Multiplexer #(.enable("false"), .select(2), .width(32)) multiplexer_6 (
    .in0(MemWriteData), .in1(32'h4), .in2(signextend_1_out32), .in3(shiftl2_32bit_1_outshift32),
    .out(multiplexer_6_out), .sel(ALUSrcB));
  ALU alu_1 (
    .A(multiplexer_5_out), .B(multiplexer_6_out), .ALUFunct(alucontrol_1_alufunct), .Overflow(Overflow),
    .Zero(Zero), .ALUOut(ALUOut));
  ALUControl alucontrol_1 (.ALUOp(ALUOp), .Funct(Instruction5_0), .ALUFunct(alucontrol_1_alufunct));
  Clock clock_6 (.out(clock_6_out));
  Register #(.width(32)) u_ALUOut (.D(ALUOut), .en(1'b1), .clk(clock_6_out), .Q(ALUOutR));  // open: clr
  Multiplexer #(.enable("false"), .width(32)) multiplexer_7 (
    .in0({32{1'b0}}), .in1(32'h1), .out(multiplexer_7_out), .sel(IntCause));
  Register #(.width(32)) EPC (.D(ALUOut), .en(EPCWrite), .clk(clock_7_out));  // open: Q, clr
  Clock clock_7 (.out(clock_7_out));
  Register #(.width(32)) Cause (.D(multiplexer_7_out), .en(CauseWrite), .clk(clock_8_out));  // open: Q, clr
  Clock clock_8 (.out(clock_8_out));

  // Other names for the same wires on the sheet: Instruction15_0[5:0] = Instruction5_0;
  //   Instruction25_0[20:0] = {Instruction20_16, Instruction15_0, Instruction5_0};
  //   Instruction15_11[4:0] = Instruction15_0[15:11]; Instruction25_21[4:0] = Instruction25_0
endmodule

module ALU (
  input  [31:0] A,
  input  [31:0] B,
  input  [1:0] ALUFunct,
  output Overflow,
  output Zero,
  output [31:0] ALUOut
);

  wire [0:0] comparator_1_lt;
  wire [31:0] adder_1_out, and_1_out, subtractor_1_out;

  Adder #(.width(32)) adder_1 (.a(A), .b(B), .out(adder_1_out), .cout(Overflow));  // open: cin
  Subtractor #(.width(32)) subtractor_1 (.a(A), .b(B), .out(subtractor_1_out));  // open: bin, bout
  assign and_1_out = A & B;  // AND_Gate and_1, 32 bits wide
  Comparator #(.width(32)) comparator_1 (.a(A), .b(B), .lt(comparator_1_lt[0]));  // open: gt, eq
  Multiplexer #(.enable("false"), .select(2), .width(32)) multiplexer_1 (
    .in0(adder_1_out), .in1(subtractor_1_out), .in2(and_1_out), .in3({{31{1'b0}}, comparator_1_lt[0]}),
    .out(ALUOut), .sel(ALUFunct));
  Comparator #(.width(32)) comparator_2 (.a(adder_1_out), .b({32{1'b0}}), .eq(Zero));  // open: gt, lt
endmodule

module ALUControl (
  input  [1:0] ALUOp,
  input  [5:0] Funct,
  output [1:0] ALUFunct
);

  wire and_1_out, and_2_out, and_3_out, not_1_out;

  not not_1 (not_1_out, Funct[0]);
  and and_1 (and_1_out, ALUOp[1], Funct[2]);
  and and_2 (and_2_out, ALUOp[1], Funct[3]);
  and and_3 (and_3_out, Funct[1], not_1_out);
  or or_1 (ALUFunct[1], and_1_out, and_2_out);
  or or_2 (ALUFunct[0], and_3_out, ALUOp[0]);
endmodule

module RegisterFile (
  input  WriteEnable,
  input  [4:0] WriteRegister,
  input  [31:0] WriteData,
  input  [4:0] ReadRegister1,
  input  [4:0] ReadRegister2,
  output [31:0] ReadData1,
  output [31:0] ReadData2
);

  wire and_1_out, and_2_out, and_3_out, and_4_out, and_5_out, and_6_out, and_7_out, and_8_out, and_9_out,
       and_10_out, and_11_out, and_12_out, and_13_out, and_14_out, and_15_out, and_16_out, and_17_out,
       and_18_out, and_19_out, and_20_out, and_21_out, and_22_out, and_23_out, and_24_out, and_25_out,
       and_26_out, and_27_out, and_28_out, and_29_out, and_30_out, and_31_out, and_32_out, clock_1_out,
       clock_2_out, clock_3_out, clock_4_out, clock_5_out, clock_6_out, clock_7_out, clock_8_out,
       clock_9_out, clock_10_out, clock_11_out, clock_12_out, clock_13_out, clock_14_out, clock_15_out,
       clock_16_out, clock_17_out, clock_18_out, clock_19_out, clock_20_out, clock_21_out, clock_22_out,
       clock_23_out, clock_24_out, clock_25_out, clock_26_out, clock_27_out, clock_28_out, clock_29_out,
       clock_30_out, clock_31_out, clock_32_out, decoder_1_out0, decoder_1_out1, decoder_1_out2,
       decoder_1_out3, decoder_1_out4, decoder_1_out5, decoder_1_out6, decoder_1_out7, decoder_1_out8,
       decoder_1_out9, decoder_1_out10, decoder_1_out11, decoder_1_out12, decoder_1_out13, decoder_1_out14,
       decoder_1_out15, decoder_1_out16, decoder_1_out17, decoder_1_out18, decoder_1_out19, decoder_1_out20,
       decoder_1_out21, decoder_1_out22, decoder_1_out23, decoder_1_out24, decoder_1_out25, decoder_1_out26,
       decoder_1_out27, decoder_1_out28, decoder_1_out29, decoder_1_out30;
  wire [31:0] register_1_q, register_2_q, register_3_q, register_4_q, register_5_q, register_6_q,
       register_7_q, register_8_q, register_9_q, register_10_q, register_11_q, register_12_q, register_13_q,
       register_14_q, register_15_q, register_16_q, register_17_q, register_18_q, register_19_q,
       register_20_q, register_21_q, register_22_q, register_23_q, register_24_q, register_25_q,
       register_26_q, register_27_q, register_28_q, register_29_q, register_30_q, register_31_q,
       register_32_q;

  Decoder #(.select(5)) decoder_1 (
    .out0(decoder_1_out0), .out1(decoder_1_out1), .out2(decoder_1_out2), .out3(decoder_1_out3),
    .out4(decoder_1_out4), .out5(decoder_1_out5), .out6(decoder_1_out6), .out7(decoder_1_out7),
    .out8(decoder_1_out8), .out9(decoder_1_out9), .out10(decoder_1_out10), .out11(decoder_1_out11),
    .out12(decoder_1_out12), .out13(decoder_1_out13), .out14(decoder_1_out14), .out15(decoder_1_out15),
    .out16(decoder_1_out16), .out17(decoder_1_out17), .out18(decoder_1_out18), .out19(decoder_1_out19),
    .out20(decoder_1_out20), .out21(decoder_1_out21), .out22(decoder_1_out22), .out23(decoder_1_out23),
    .out24(decoder_1_out24), .out25(decoder_1_out25), .out26(decoder_1_out26), .out27(decoder_1_out27),
    .out28(decoder_1_out28), .out29(decoder_1_out29), .out30(decoder_1_out30), .out31(decoder_1_out30),
    .sel(WriteRegister));  // open: en
  and and_1 (and_1_out, decoder_1_out0, WriteEnable);
  and and_2 (and_2_out, decoder_1_out1, WriteEnable);
  and and_3 (and_3_out, decoder_1_out2, WriteEnable);
  and and_4 (and_4_out, decoder_1_out3, WriteEnable);
  and and_5 (and_5_out, decoder_1_out4, WriteEnable);
  and and_6 (and_6_out, decoder_1_out5, WriteEnable);
  and and_7 (and_7_out, decoder_1_out6, WriteEnable);
  and and_8 (and_8_out, decoder_1_out7, WriteEnable);
  and and_9 (and_9_out, decoder_1_out8, WriteEnable);
  and and_10 (and_10_out, decoder_1_out9, WriteEnable);
  and and_11 (and_11_out, decoder_1_out10, WriteEnable);
  and and_12 (and_12_out, decoder_1_out11, WriteEnable);
  and and_13 (and_13_out, decoder_1_out12, WriteEnable);
  and and_14 (and_14_out, decoder_1_out13, WriteEnable);
  and and_15 (and_15_out, decoder_1_out14, WriteEnable);
  and and_16 (and_16_out, decoder_1_out15, WriteEnable);
  and and_17 (and_17_out, decoder_1_out16, WriteEnable);
  and and_18 (and_18_out, decoder_1_out17, WriteEnable);
  and and_19 (and_19_out, decoder_1_out18, WriteEnable);
  and and_20 (and_20_out, decoder_1_out19, WriteEnable);
  and and_21 (and_21_out, decoder_1_out20, WriteEnable);
  and and_22 (and_22_out, decoder_1_out21, WriteEnable);
  and and_23 (and_23_out, decoder_1_out22, WriteEnable);
  and and_24 (and_24_out, decoder_1_out23, WriteEnable);
  and and_25 (and_25_out, decoder_1_out24, WriteEnable);
  and and_26 (and_26_out, decoder_1_out25, WriteEnable);
  and and_27 (and_27_out, decoder_1_out26, WriteEnable);
  and and_28 (and_28_out, decoder_1_out27, WriteEnable);
  and and_29 (and_29_out, decoder_1_out28, WriteEnable);
  and and_30 (and_30_out, decoder_1_out29, WriteEnable);
  and and_31 (and_31_out, decoder_1_out30, WriteEnable);
  and and_32 (and_32_out, decoder_1_out30, WriteEnable);
  Register #(.width(32)) register_1 (.D(WriteData), .en(and_1_out), .clk(clock_1_out), .Q(register_1_q));  // open: clr
  Clock clock_1 (.out(clock_1_out));
  Register #(.width(32)) register_2 (.D(WriteData), .en(and_2_out), .clk(clock_2_out), .Q(register_2_q));  // open: clr
  Clock clock_2 (.out(clock_2_out));
  Register #(.width(32)) register_3 (.D(WriteData), .en(and_3_out), .clk(clock_3_out), .Q(register_3_q));  // open: clr
  Clock clock_3 (.out(clock_3_out));
  Register #(.width(32)) register_4 (.D(WriteData), .en(and_4_out), .clk(clock_4_out), .Q(register_4_q));  // open: clr
  Clock clock_4 (.out(clock_4_out));
  Register #(.width(32)) register_5 (.D(WriteData), .en(and_5_out), .clk(clock_5_out), .Q(register_5_q));  // open: clr
  Clock clock_5 (.out(clock_5_out));
  Register #(.width(32)) register_6 (.D(WriteData), .en(and_6_out), .clk(clock_6_out), .Q(register_6_q));  // open: clr
  Clock clock_6 (.out(clock_6_out));
  Register #(.width(32)) register_7 (.D(WriteData), .en(and_7_out), .clk(clock_7_out), .Q(register_7_q));  // open: clr
  Clock clock_7 (.out(clock_7_out));
  Register #(.width(32)) register_8 (.D(WriteData), .en(and_8_out), .clk(clock_8_out), .Q(register_8_q));  // open: clr
  Clock clock_8 (.out(clock_8_out));
  Register #(.width(32)) register_9 (.D(WriteData), .en(and_9_out), .clk(clock_9_out), .Q(register_9_q));  // open: clr
  Clock clock_9 (.out(clock_9_out));
  Register #(.width(32)) register_10 (
    .D(WriteData), .en(and_10_out), .clk(clock_10_out), .Q(register_10_q));  // open: clr
  Clock clock_10 (.out(clock_10_out));
  Register #(.width(32)) register_11 (
    .D(WriteData), .en(and_11_out), .clk(clock_11_out), .Q(register_11_q));  // open: clr
  Clock clock_11 (.out(clock_11_out));
  Register #(.width(32)) register_12 (
    .D(WriteData), .en(and_12_out), .clk(clock_12_out), .Q(register_12_q));  // open: clr
  Clock clock_12 (.out(clock_12_out));
  Register #(.width(32)) register_13 (
    .D(WriteData), .en(and_13_out), .clk(clock_13_out), .Q(register_13_q));  // open: clr
  Clock clock_13 (.out(clock_13_out));
  Register #(.width(32)) register_14 (
    .D(WriteData), .en(and_14_out), .clk(clock_14_out), .Q(register_14_q));  // open: clr
  Clock clock_14 (.out(clock_14_out));
  Register #(.width(32)) register_15 (
    .D(WriteData), .en(and_15_out), .clk(clock_15_out), .Q(register_15_q));  // open: clr
  Clock clock_15 (.out(clock_15_out));
  Register #(.width(32)) register_16 (
    .D(WriteData), .en(and_16_out), .clk(clock_16_out), .Q(register_16_q));  // open: clr
  Clock clock_16 (.out(clock_16_out));
  Register #(.width(32)) register_17 (
    .D(WriteData), .en(and_17_out), .clk(clock_17_out), .Q(register_17_q));  // open: clr
  Clock clock_17 (.out(clock_17_out));
  Register #(.width(32)) register_18 (
    .D(WriteData), .en(and_18_out), .clk(clock_18_out), .Q(register_18_q));  // open: clr
  Clock clock_18 (.out(clock_18_out));
  Register #(.width(32)) register_19 (
    .D(WriteData), .en(and_19_out), .clk(clock_19_out), .Q(register_19_q));  // open: clr
  Clock clock_19 (.out(clock_19_out));
  Register #(.width(32)) register_20 (
    .D(WriteData), .en(and_20_out), .clk(clock_20_out), .Q(register_20_q));  // open: clr
  Clock clock_20 (.out(clock_20_out));
  Register #(.width(32)) register_21 (
    .D(WriteData), .en(and_21_out), .clk(clock_21_out), .Q(register_21_q));  // open: clr
  Clock clock_21 (.out(clock_21_out));
  Register #(.width(32)) register_22 (
    .D(WriteData), .en(and_22_out), .clk(clock_22_out), .Q(register_22_q));  // open: clr
  Clock clock_22 (.out(clock_22_out));
  Register #(.width(32)) register_23 (
    .D(WriteData), .en(and_23_out), .clk(clock_23_out), .Q(register_23_q));  // open: clr
  Clock clock_23 (.out(clock_23_out));
  Register #(.width(32)) register_24 (
    .D(WriteData), .en(and_24_out), .clk(clock_24_out), .Q(register_24_q));  // open: clr
  Clock clock_24 (.out(clock_24_out));
  Register #(.width(32)) register_25 (
    .D(WriteData), .en(and_25_out), .clk(clock_25_out), .Q(register_25_q));  // open: clr
  Clock clock_25 (.out(clock_25_out));
  Register #(.width(32)) register_26 (
    .D(WriteData), .en(and_26_out), .clk(clock_26_out), .Q(register_26_q));  // open: clr
  Clock clock_26 (.out(clock_26_out));
  Register #(.width(32)) register_27 (
    .D(WriteData), .en(and_27_out), .clk(clock_27_out), .Q(register_27_q));  // open: clr
  Clock clock_27 (.out(clock_27_out));
  Register #(.width(32)) register_28 (
    .D(WriteData), .en(and_28_out), .clk(clock_28_out), .Q(register_28_q));  // open: clr
  Clock clock_28 (.out(clock_28_out));
  Register #(.width(32)) register_29 (
    .D(WriteData), .en(and_29_out), .clk(clock_29_out), .Q(register_29_q));  // open: clr
  Clock clock_29 (.out(clock_29_out));
  Register #(.width(32)) register_30 (
    .D(WriteData), .en(and_30_out), .clk(clock_30_out), .Q(register_30_q));  // open: clr
  Clock clock_30 (.out(clock_30_out));
  Register #(.width(32)) register_31 (
    .D(WriteData), .en(and_31_out), .clk(clock_31_out), .Q(register_31_q));  // open: clr
  Clock clock_31 (.out(clock_31_out));
  Register #(.width(32)) register_32 (
    .D(WriteData), .en(and_32_out), .clk(clock_32_out), .Q(register_32_q));  // open: clr
  Clock clock_32 (.out(clock_32_out));
  Multiplexer #(.enable("false"), .select(5), .width(32)) multiplexer_1 (
    .in0(register_1_q), .in1(register_2_q), .in2(register_3_q), .in3(register_4_q), .in4(register_5_q),
    .in5(register_6_q), .in6(register_7_q), .in7(register_8_q), .in8(register_9_q), .in9(register_10_q),
    .in10(register_11_q), .in11(register_12_q), .in12(register_13_q), .in13(register_14_q),
    .in14(register_15_q), .in15(register_16_q), .in16(register_17_q), .in17(register_18_q),
    .in18(register_19_q), .in19(register_20_q), .in20(register_21_q), .in21(register_22_q),
    .in22(register_23_q), .in23(register_24_q), .in24(register_25_q), .in25(register_26_q),
    .in26(register_27_q), .in27(register_28_q), .in28(register_29_q), .in29(register_30_q),
    .in30(register_31_q), .in31(register_32_q), .out(ReadData1), .sel(ReadRegister1));
  Multiplexer #(.enable("false"), .select(5), .width(32)) multiplexer_2 (
    .in0(register_1_q), .in1(register_2_q), .in2(register_3_q), .in3(register_4_q), .in4(register_5_q),
    .in5(register_6_q), .in6(register_7_q), .in7(register_8_q), .in8(register_9_q), .in9(register_10_q),
    .in10(register_11_q), .in11(register_12_q), .in12(register_13_q), .in13(register_14_q),
    .in14(register_15_q), .in15(register_16_q), .in16(register_17_q), .in17(register_18_q),
    .in18(register_19_q), .in19(register_20_q), .in20(register_21_q), .in21(register_22_q),
    .in22(register_23_q), .in23(register_24_q), .in24(register_25_q), .in25(register_26_q),
    .in26(register_27_q), .in27(register_28_q), .in28(register_29_q), .in29(register_30_q),
    .in30(register_31_q), .in31(register_32_q), .out(ReadData2), .sel(ReadRegister2));
endmodule

module Memory (
  input  [31:0] MemAddr,
  input  MemWrite,
  input  MemRead,
  input  [31:0] MemWriteData,
  output [31:0] MemData
);

  wire clock_1_out;
  wire [31:0] ram_1_dout;

  Clock clock_1 (.out(clock_1_out));
  RAM #(.addrWidth(24), .dataWidth(32), .enables("line"), .\type ("nonvolatile")) ram_1 (
    .addr(MemAddr[25:2]), .we(MemWrite), .clk(clock_1_out), .din(MemWriteData), .dout(ram_1_dout));
  Register #(.trigger("high"), .width(32)) register_1 (
    .D(ram_1_dout), .en(MemRead), .clk(1'b1), .Q(MemData));  // open: clr
endmodule

module SignExtend (
  input  [15:0] In16,
  output [31:0] Out32
);


  assign Out32 = {{17{In16[15]}}, In16[14:0]};
endmodule

module ShiftL2_32bit (
  input  [31:0] In32,
  output [31:0] OutShift32
);

  Shifter #(.width(32)) shifter_1 (.in(In32), .\dist (5'b00010), .out(OutShift32));
endmodule

module ShiftLeft26BitTo28 (
  input  [25:0] In26,
  output [27:0] Out28
);


  assign Out28 = {In26, 2'b00};
endmodule

module ControlUnit (
  input  [5:0] Op,
  input  Overflow,
  output PCWriteCond,
  output PCWrite,
  output IorD,
  output MemRead,
  output MemWrite,
  output MemtoReg,
  output IRWrite,
  output CauseWrite,
  output IntCause,
  output EPCWrite,
  output [1:0] PCSource,
  output [1:0] ALUOp,
  output ALUSrcA,
  output [1:0] ALUSrcB,
  output RegWrite,
  output RegDst
);

  wire and_2_out, and_3_out, and_4_out, and_6_out, and_7_out, and_13_out, and_14_out, and_15_out, and_16_out,
       and_18_out, and_19_out, and_20_out, and_21_out, and_22_out, and_23_out, and_24_out, and_25_out,
       and_26_out, and_27_out, and_29_out, and_30_out, and_31_out, and_32_out, and_33_out, and_34_out,
       and_35_out, and_36_out, and_37_out, and_38_out, and_39_out, and_40_out, and_41_out, and_42_out,
       and_43_out, and_44_out, and_45_out, and_46_out, and_47_out, and_48_out, and_49_out, and_50_out,
       and_51_out, and_52_out, and_53_out, clock_1_out, not_1_out, not_2_out, not_3_out, not_4_out,
       not_5_out, not_6_out, not_7_out, not_8_out, not_9_out, not_10_out;
  wire [3:0] or_13_out, StateReg_q;

  not not_1 (not_1_out, StateReg_q[3]);
  not not_2 (not_2_out, StateReg_q[2]);
  not not_3 (not_3_out, StateReg_q[1]);
  not not_4 (not_4_out, StateReg_q[0]);
  not not_5 (not_5_out, Op[5]);
  not not_6 (not_6_out, Op[4]);
  not not_7 (not_7_out, Op[3]);
  not not_8 (not_8_out, Op[2]);
  not not_9 (not_9_out, Op[1]);
  not not_10 (not_10_out, Op[0]);
  Clock clock_1 (.out(clock_1_out));
  Register #(.width(4)) StateReg (.D(or_13_out), .en(1'b1), .clk(clock_1_out), .Q(StateReg_q));  // open: clr
  and and_1 (PCWriteCond, StateReg_q[3], not_3_out, not_4_out);
  and and_2 (and_2_out, not_1_out, not_2_out, not_3_out, not_4_out);
  and and_3 (and_3_out, StateReg_q[3], StateReg_q[0]);
  and and_4 (and_4_out, StateReg_q[3], StateReg_q[1]);
  and and_5 (IorD, not_1_out, not_2_out, StateReg_q[1], StateReg_q[0]);
  and and_6 (and_6_out, not_1_out, not_2_out, not_3_out, not_4_out);
  and and_7 (and_7_out, not_1_out, not_2_out, StateReg_q[1], StateReg_q[0]);
  and and_8 (MemtoReg, StateReg_q[2], not_3_out, not_4_out);
  and and_9 (IRWrite, not_1_out, not_2_out, not_3_out, not_4_out);
  and and_10 (CauseWrite, StateReg_q[3], StateReg_q[1]);
  and and_11 (IntCause, StateReg_q[3], StateReg_q[1], StateReg_q[0]);
  and and_12 (EPCWrite, StateReg_q[3], StateReg_q[1]);
  and and_13 (and_13_out, StateReg_q[3], StateReg_q[0]);
  and and_14 (and_14_out, StateReg_q[3], StateReg_q[1]);
  and and_15 (and_15_out, StateReg_q[3], not_4_out);
  and and_16 (and_16_out, StateReg_q[3], StateReg_q[1]);
  and and_17 (ALUOp[1], StateReg_q[2], StateReg_q[1], not_4_out);
  and and_18 (and_18_out, StateReg_q[3], not_4_out);
  and and_19 (and_19_out, StateReg_q[3], StateReg_q[1]);
  and and_20 (and_20_out, not_1_out, StateReg_q[1], not_4_out);
  and and_21 (and_21_out, StateReg_q[3], not_3_out, not_4_out);
  and and_22 (and_22_out, not_1_out, not_2_out, not_3_out, StateReg_q[0]);
  and and_23 (and_23_out, not_1_out, not_2_out, StateReg_q[1], not_4_out);
  and and_24 (and_24_out, not_1_out, not_2_out, not_3_out);
  and and_25 (and_25_out, StateReg_q[3], StateReg_q[1]);
  and and_26 (and_26_out, StateReg_q[2], not_3_out, not_4_out);
  and and_27 (and_27_out, StateReg_q[2], StateReg_q[1], StateReg_q[0]);
  and and_28 (RegDst, StateReg_q[2], StateReg_q[1], StateReg_q[0]);
  and and_29 (and_29_out, not_1_out, not_2_out, not_3_out, StateReg_q[0], not_9_out, Op[0]);
  and and_30 (and_30_out, not_1_out, not_2_out, not_3_out, StateReg_q[0], not_5_out, Op[1]);
  and and_31 (and_31_out, not_1_out, not_2_out, not_3_out, StateReg_q[0], Op[1], not_10_out);
  and and_32 (and_32_out, not_1_out, not_2_out, not_3_out, StateReg_q[0], Op[2]);
  and and_33 (and_33_out, not_1_out, not_2_out, not_3_out, StateReg_q[0], Op[3], not_9_out);
  and and_34 (and_34_out, not_1_out, not_2_out, not_3_out, StateReg_q[0], Op[4]);
  and and_35 (and_35_out, not_1_out, not_2_out, not_3_out, StateReg_q[0], Op[5], not_9_out);
  and and_36 (and_36_out, StateReg_q[2], StateReg_q[1], StateReg_q[0], Overflow);
  and and_37 (and_37_out, not_1_out, not_2_out, StateReg_q[0], not_5_out, not_6_out, not_7_out, not_8_out, not_9_out, not_10_out);
  and and_38 (and_38_out, not_1_out, StateReg_q[1], not_4_out, Op[3]);
  and and_39 (and_39_out, not_1_out, not_2_out, StateReg_q[1], StateReg_q[0]);
  and and_40 (and_40_out, StateReg_q[2], StateReg_q[1], not_4_out);
  and and_41 (and_41_out, not_1_out, not_2_out, not_3_out, StateReg_q[0], not_8_out, not_9_out);
  and and_42 (and_42_out, not_1_out, not_2_out, not_3_out, StateReg_q[0], Op[0]);
  and and_43 (and_43_out, not_1_out, not_2_out, not_3_out, StateReg_q[0], Op[2], Op[1]);
  and and_44 (and_44_out, not_1_out, not_2_out, not_3_out, StateReg_q[0], Op[3]);
  and and_45 (and_45_out, not_1_out, not_2_out, not_3_out, StateReg_q[0], Op[4]);
  and and_46 (and_46_out, not_1_out, not_2_out, not_3_out, StateReg_q[0], Op[5]);
  and and_47 (and_47_out, not_1_out, StateReg_q[1], not_4_out, not_7_out);
  and and_48 (and_48_out, StateReg_q[2], StateReg_q[1], not_4_out);
  and and_49 (and_49_out, StateReg_q[2], StateReg_q[1], Overflow);
  and and_50 (and_50_out, not_1_out, not_2_out, not_4_out);
  and and_51 (and_51_out, not_1_out, not_2_out, not_3_out, not_5_out, not_6_out, not_7_out, not_8_out, Op[1], not_10_out);
  and and_52 (and_52_out, not_1_out, StateReg_q[1], not_4_out);
  and and_53 (and_53_out, StateReg_q[2], StateReg_q[1], Overflow);
  or or_1 (PCWrite, and_2_out, and_3_out, and_4_out);
  or or_2 (MemRead, and_6_out, and_7_out);
  or or_3 (PCSource[1], and_13_out, and_14_out);
  or or_4 (PCSource[0], and_15_out, and_16_out);
  or or_5 (ALUOp[0], and_18_out, and_19_out);
  or or_6 (ALUSrcA, and_20_out, and_21_out);
  or or_7 (ALUSrcB[1], and_22_out, and_23_out);
  or or_8 (ALUSrcB[0], and_24_out, and_25_out);
  or or_9 (RegWrite, and_26_out, and_27_out);
  or or_10 (or_13_out[3], and_29_out, and_30_out, and_31_out, and_32_out, and_33_out, and_34_out, and_35_out, and_36_out);
  or or_11 (or_13_out[2], and_37_out, and_38_out, and_39_out, and_40_out);
  or or_12 (or_13_out[1], and_41_out, and_42_out, and_43_out, and_44_out, and_45_out, and_46_out, and_47_out, and_48_out, and_49_out);
  or or_13 (or_13_out[0], and_50_out, and_51_out, and_52_out, and_53_out);

  assign MemWrite = 1'b0;

  // Notes on the sheet:
  //   Next State
endmodule

module ControlUnit1 (
  input  [5:0] Op,
  input  Overflow,
  output PCWriteCond,
  output PCWrite,
  output IorD,
  output MemRead,
  output MemWrite,
  output MemtoReg,
  output IRWrite,
  output CauseWrite,
  output IntCause,
  output EPCWrite,
  output [1:0] PCSource,
  output [1:0] ALUOp,
  output ALUSrcA,
  output [1:0] ALUSrcB,
  output RegWrite,
  output RegDst
);

  wire and_2_out, and_3_out, and_4_out, and_5_out, and_6_out, and_7_out, and_8_out, and_15_out, and_16_out,
       and_17_out, and_18_out, and_20_out, and_21_out, and_22_out, and_23_out, and_24_out, and_25_out,
       and_26_out, and_27_out, and_28_out, and_29_out, and_31_out, and_32_out, and_33_out, and_34_out,
       and_35_out, and_36_out, and_37_out, and_38_out, and_39_out, and_40_out, and_41_out, and_42_out,
       and_43_out, and_44_out, and_45_out, and_46_out, and_47_out, and_48_out, and_49_out, and_50_out,
       and_51_out, and_52_out, and_53_out, and_54_out, and_55_out, clock_1_out, not_1_out, not_2_out,
       not_3_out, not_4_out, not_5_out, not_6_out, not_7_out, not_8_out, not_9_out, not_10_out;
  wire [3:0] or_14_out, StateReg_q;

  not not_1 (not_1_out, StateReg_q[3]);
  not not_2 (not_2_out, StateReg_q[2]);
  not not_3 (not_3_out, StateReg_q[1]);
  not not_4 (not_4_out, StateReg_q[0]);
  not not_5 (not_5_out, Op[5]);
  not not_6 (not_6_out, Op[4]);
  not not_7 (not_7_out, Op[3]);
  not not_8 (not_8_out, Op[2]);
  not not_9 (not_9_out, Op[1]);
  not not_10 (not_10_out, Op[0]);
  Register #(.width(4)) StateReg (.D(or_14_out), .en(1'b1), .clk(clock_1_out), .Q(StateReg_q));  // open: clr
  Clock clock_1 (.out(clock_1_out));
  and and_1 (PCWriteCond, StateReg_q[3], not_3_out, not_4_out);
  and and_2 (and_2_out, not_1_out, not_2_out, not_3_out, not_4_out);
  and and_3 (and_3_out, StateReg_q[3], StateReg_q[0]);
  and and_4 (and_4_out, StateReg_q[3], StateReg_q[1]);
  and and_5 (and_5_out, not_1_out, not_2_out, StateReg_q[1], StateReg_q[0]);
  and and_6 (and_6_out, StateReg_q[2], not_3_out, StateReg_q[0]);
  and and_7 (and_7_out, not_1_out, not_2_out, not_3_out, not_4_out);
  and and_8 (and_8_out, not_1_out, not_2_out, StateReg_q[1], StateReg_q[0]);
  and and_9 (MemWrite, StateReg_q[2], not_3_out, StateReg_q[0]);
  and and_10 (MemtoReg, StateReg_q[2], not_3_out, not_4_out);
  and and_11 (IRWrite, not_1_out, not_2_out, not_3_out, not_4_out);
  and and_12 (CauseWrite, StateReg_q[3], StateReg_q[1]);
  and and_13 (IntCause, StateReg_q[3], StateReg_q[1], StateReg_q[0]);
  and and_14 (EPCWrite, StateReg_q[3], StateReg_q[1]);
  and and_15 (and_15_out, StateReg_q[3], StateReg_q[0]);
  and and_16 (and_16_out, StateReg_q[3], StateReg_q[1]);
  and and_17 (and_17_out, StateReg_q[3], not_4_out);
  and and_18 (and_18_out, StateReg_q[3], StateReg_q[1]);
  and and_19 (ALUOp[1], StateReg_q[2], StateReg_q[1], not_4_out);
  and and_20 (and_20_out, StateReg_q[3], not_4_out);
  and and_21 (and_21_out, StateReg_q[3], StateReg_q[1]);
  and and_22 (and_22_out, not_1_out, StateReg_q[1], not_4_out);
  and and_23 (and_23_out, StateReg_q[3], not_3_out, not_4_out);
  and and_24 (and_24_out, not_1_out, not_2_out, not_3_out, StateReg_q[0]);
  and and_25 (and_25_out, not_1_out, not_2_out, StateReg_q[1], not_4_out);
  and and_26 (and_26_out, not_1_out, not_2_out, not_3_out);
  and and_27 (and_27_out, StateReg_q[3], StateReg_q[1]);
  and and_28 (and_28_out, StateReg_q[2], not_3_out, not_4_out);
  and and_29 (and_29_out, StateReg_q[2], StateReg_q[1], StateReg_q[0]);
  and and_30 (RegDst, StateReg_q[2], StateReg_q[1], StateReg_q[0]);
  and and_31 (and_31_out, not_1_out, not_2_out, not_3_out, StateReg_q[0], not_9_out, Op[0]);
  and and_32 (and_32_out, not_1_out, not_2_out, not_3_out, StateReg_q[0], not_5_out, Op[1]);
  and and_33 (and_33_out, not_1_out, not_2_out, not_3_out, StateReg_q[0], Op[1], not_10_out);
  and and_34 (and_34_out, not_1_out, not_2_out, not_3_out, StateReg_q[0], Op[2]);
  and and_35 (and_35_out, not_1_out, not_2_out, not_3_out, StateReg_q[0], Op[3], not_9_out);
  and and_36 (and_36_out, not_1_out, not_2_out, not_3_out, StateReg_q[0], Op[4]);
  and and_37 (and_37_out, not_1_out, not_2_out, not_3_out, StateReg_q[0], Op[5], not_9_out);
  and and_38 (and_38_out, StateReg_q[2], StateReg_q[1], StateReg_q[0], Overflow);
  and and_39 (and_39_out, not_1_out, not_2_out, StateReg_q[0], not_5_out, not_6_out, not_7_out, not_8_out, not_9_out, not_10_out);
  and and_40 (and_40_out, not_1_out, StateReg_q[1], not_4_out, Op[3]);
  and and_41 (and_41_out, not_1_out, not_2_out, StateReg_q[1], StateReg_q[0]);
  and and_42 (and_42_out, StateReg_q[2], StateReg_q[1], not_4_out);
  and and_43 (and_43_out, not_1_out, not_2_out, not_3_out, StateReg_q[0], not_8_out, not_9_out);
  and and_44 (and_44_out, not_1_out, not_2_out, not_3_out, StateReg_q[0], Op[0]);
  and and_45 (and_45_out, not_1_out, not_2_out, not_3_out, StateReg_q[0], Op[2], Op[1]);
  and and_46 (and_46_out, not_1_out, not_2_out, not_3_out, StateReg_q[0], Op[3]);
  and and_47 (and_47_out, not_1_out, not_2_out, not_3_out, StateReg_q[0], Op[4]);
  and and_48 (and_48_out, not_1_out, not_2_out, not_3_out, StateReg_q[0], Op[5]);
  and and_49 (and_49_out, not_1_out, StateReg_q[1], not_4_out, not_7_out);
  and and_50 (and_50_out, StateReg_q[2], StateReg_q[1], not_4_out);
  and and_51 (and_51_out, StateReg_q[2], StateReg_q[1], Overflow);
  and and_52 (and_52_out, not_1_out, not_2_out, not_4_out);
  and and_53 (and_53_out, not_1_out, not_2_out, not_3_out, not_5_out, not_6_out, not_7_out, not_8_out, Op[1], not_10_out);
  and and_54 (and_54_out, not_1_out, StateReg_q[1], not_4_out);
  and and_55 (and_55_out, StateReg_q[2], StateReg_q[1], Overflow);
  or or_1 (PCWrite, and_2_out, and_3_out, and_4_out);
  or or_2 (IorD, and_5_out, and_6_out);
  or or_3 (MemRead, and_7_out, and_8_out);
  or or_4 (PCSource[1], and_15_out, and_16_out);
  or or_5 (PCSource[0], and_17_out, and_18_out);
  or or_6 (ALUOp[0], and_20_out, and_21_out);
  or or_7 (ALUSrcA, and_22_out, and_23_out);
  or or_8 (ALUSrcB[1], and_24_out, and_25_out);
  or or_9 (ALUSrcB[0], and_26_out, and_27_out);
  or or_10 (RegWrite, and_28_out, and_29_out);
  or or_11 (or_14_out[3], and_31_out, and_32_out, and_33_out, and_34_out, and_35_out, and_36_out, and_37_out, and_38_out);
  or or_12 (or_14_out[2], and_39_out, and_40_out, and_41_out, and_42_out);
  or or_13 (or_14_out[1], and_43_out, and_44_out, and_45_out, and_46_out, and_47_out, and_48_out, and_49_out, and_50_out, and_51_out);
  or or_14 (or_14_out[0], and_52_out, and_53_out, and_54_out, and_55_out);
endmodule
