// Logisim project MIPS_MultiCycle.circ as structural Verilog: 12 circuits, main circuit Datapath
module Datapath (
);

  wire and_1_out, CauseWrite, CLK, EPCWrite, IntCause, IorD, IRWrite, MemRead, MemtoReg, MemWrite, or_1_out,
       Overflow, PCWrite, PCWriteCond, ReadSrc, RegDst, RegWrite, Zero;
  wire [1:0] alucontrol_1_alufunct, ALUOp, ALUSrcA, ALUSrcB, PCSource;
  wire [4:0] Instruction4_0, Instruction20_16, multiplexer_2_out, multiplexer_3_out;
  wire [5:0] Instruction31_26;
  wire [5:5] Instruction5_0;
  wire [15:6] Instruction15_0;
  wire [25:21] Instruction25_0;
  wire [27:0] shiftleft26bitto28_1_out28;
  wire [31:0] A_q, ALUOut, ALUOutR, memory_1_memdata, MemoryDataReg, MemWriteData, multiplexer_1_out,
       multiplexer_4_out, multiplexer_5_out, multiplexer_6_out, multiplexer_7_out, multiplexer_8_out, PC,
       RegFile_readdata1, RegFile_readdata2, shiftl2_32bit_1_outshift32, signextend_1_out32;

  Clock u_CLK (.out(CLK));
  ShiftLeft26BitTo28 shiftleft26bitto28_1 (
    .In26({Instruction25_0, Instruction20_16, Instruction15_0, Instruction5_0[5], Instruction4_0}),
    .Out28(shiftleft26bitto28_1_out28));
  Multiplexer #(.enable("false"), .select(2), .width(32)) multiplexer_1 (
    .in0(ALUOut), .in1(ALUOutR), .in2({PC[31:28], shiftleft26bitto28_1_out28}), .in3(32'h80000180),
    .out(multiplexer_1_out), .sel(PCSource));
  Multiplexer #(.enable("false"), .width(5)) multiplexer_2 (
    .in0(Instruction20_16), .in1(Instruction4_0), .out(multiplexer_2_out), .sel(ReadSrc));
  or or_1 (or_1_out, and_1_out, PCWrite);
  Multiplexer #(.enable("false"), .width(5)) multiplexer_3 (
    .in0(Instruction20_16), .in1(Instruction15_0[15:11]), .out(multiplexer_3_out), .sel(RegDst));
  Multiplexer #(.enable("false"), .width(32)) multiplexer_4 (
    .in0(ALUOutR), .in1(MemoryDataReg), .out(multiplexer_4_out), .sel(MemtoReg));
  and and_1 (and_1_out, Zero, PCWriteCond);
  Register #(.width(32)) u_PC (.D(multiplexer_1_out), .en(or_1_out), .clk(CLK), .Q(PC));  // open: clr
  SignExtend signextend_1 (.In16({Instruction15_0, Instruction5_0[5], Instruction4_0}), .Out32(signextend_1_out32));
  RegisterFile RegFile (
    .ReadData1(RegFile_readdata1), .ReadData2(RegFile_readdata2), .CLK(CLK),
    .ReadRegister2(multiplexer_2_out), .WriteEnable(RegWrite), .WriteRegister(multiplexer_3_out),
    .WriteData(multiplexer_4_out), .ReadRegister1(Instruction25_0));
  Multiplexer #(.enable("false"), .width(32)) multiplexer_5 (
    .in0(PC), .in1(ALUOutR), .out(multiplexer_5_out), .sel(IorD));
  Register #(.width(32)) A (.D(RegFile_readdata1), .en(1'b1), .clk(CLK), .Q(A_q));  // open: clr
  Register #(.width(32)) B (.D(RegFile_readdata2), .en(1'b1), .clk(CLK), .Q(MemWriteData));  // open: clr
  ControlUnit controlunit_1 (
    .Op(Instruction31_26), .Overflow(Overflow), .CLK(CLK), .PCWriteCond(PCWriteCond), .PCWrite(PCWrite),
    .IorD(IorD), .MemRead(MemRead), .MemWrite(MemWrite), .MemtoReg(MemtoReg), .IRWrite(IRWrite),
    .CauseWrite(CauseWrite), .IntCause(IntCause), .EPCWrite(EPCWrite), .PCSource(PCSource), .ALUOp(ALUOp),
    .ALUSrcA(ALUSrcA), .ALUSrcB(ALUSrcB), .RegWrite(RegWrite), .RegDst(RegDst), .ReadSrc(ReadSrc));
  ShiftL2_32bit shiftl2_32bit_1 (.In32(signextend_1_out32), .OutShift32(shiftl2_32bit_1_outshift32));
  Memory memory_1 (
    .MemData(memory_1_memdata), .MemRead(MemRead), .CLK(CLK), .MemAddr(multiplexer_5_out),
    .MemWriteData(MemWriteData), .MemWrite(MemWrite));
  Register #(.width(32)) MemoryDataRegister (
    .D(memory_1_memdata), .en(1'b1), .clk(CLK), .Q(MemoryDataReg));  // open: clr
  Register #(.width(32)) InstructionRegister (
    .D(memory_1_memdata), .en(IRWrite), .clk(CLK),
    .Q({Instruction31_26, Instruction25_0, Instruction20_16, Instruction15_0, Instruction5_0[5], Instruction4_0}));  // open: clr
  Multiplexer #(.enable("false"), .select(2), .width(32)) multiplexer_6 (
    .in0(PC), .in1(A_q), .in2(ALUOutR), .out(multiplexer_6_out), .sel(ALUSrcA));  // open: in3
  Multiplexer #(.enable("false"), .select(2), .width(32)) multiplexer_7 (
    .in0(MemWriteData), .in1(32'h4), .in2(signextend_1_out32), .in3(shiftl2_32bit_1_outshift32),
    .out(multiplexer_7_out), .sel(ALUSrcB));
  ALU alu_1 (
    .A(multiplexer_6_out), .B(multiplexer_7_out), .ALUFunct(alucontrol_1_alufunct), .Overflow(Overflow),
    .Zero(Zero), .ALUOut(ALUOut));
  ALUControl alucontrol_1 (
    .ALUOp(ALUOp), .Funct({Instruction5_0[5], Instruction4_0}), .ALUFunct(alucontrol_1_alufunct));
  Register #(.width(32)) u_ALUOut (.D(ALUOut), .en(1'b1), .clk(CLK), .Q(ALUOutR));  // open: clr
  Multiplexer #(.enable("false"), .width(32)) multiplexer_8 (
    .in0({32{1'b0}}), .in1(32'h1), .out(multiplexer_8_out), .sel(IntCause));
  Register #(.width(32)) EPC (.D(ALUOut), .en(EPCWrite), .clk(CLK));  // open: Q, clr
  Register #(.width(32)) Cause (.D(multiplexer_8_out), .en(CauseWrite), .clk(CLK));  // open: Q, clr

  // Other names for the same wires on the sheet: Instruction5_0[4:0] = Instruction4_0;
  //   Instruction15_0[5:0] = {Instruction5_0[5], Instruction4_0};
  //   Instruction25_0[20:0] = {Instruction20_16, Instruction15_0, Instruction5_0[5], Instruction4_0};
  //   Instruction15_11[4:0] = Instruction15_0[15:11]; Instruction25_21[4:0] = Instruction25_0
endmodule

module ALU (
  input  [31:0] A,
  input  [31:0] B,
  input  [1:0] ALUFunct,
  output Overflow,
  output Zero,
  output [31:0] ALUOut
);

  wire [0:0] comparator_1_lt;
  wire [31:0] adder_1_out, and_1_out, subtractor_1_out;

  Adder #(.width(32)) adder_1 (.a(A), .b(B), .out(adder_1_out));  // open: cin, cout
  Subtractor #(.width(32)) subtractor_1 (.a(A), .b(B), .out(subtractor_1_out));  // open: bin, bout
  assign and_1_out = A & B;  // AND_Gate and_1, 32 bits wide
  Comparator #(.width(32)) comparator_1 (.a(A), .b(B), .lt(comparator_1_lt[0]));  // open: gt, eq
  Multiplexer #(.enable("false"), .select(2), .width(32)) multiplexer_1 (
    .in0(adder_1_out), .in1(subtractor_1_out), .in2(and_1_out), .in3({{31{1'b0}}, comparator_1_lt[0]}),
    .out(ALUOut), .sel(ALUFunct));
  Comparator #(.width(32)) comparator_2 (.a(subtractor_1_out), .b({32{1'b0}}), .eq(Zero));  // open: gt, lt
  OverflowDetect overflowdetect_1 (.SignA(A[31]), .SignB(B[31]), .SignOut(ALUOut[31]), .Overflow(Overflow));
endmodule

module ALUControl (
  input  [1:0] ALUOp,
  input  [5:0] Funct,
  output [1:0] ALUFunct
);

  wire and_1_out, and_2_out, and_3_out;

  and and_1 (and_1_out, ALUOp[1], Funct[2]);
  and and_2 (and_2_out, ALUOp[1], Funct[3]);
  and and_3 (and_3_out, ALUOp[1], Funct[1]);
  or or_1 (ALUFunct[1], and_1_out, and_2_out);
  or or_2 (ALUFunct[0], ALUOp[0], and_3_out);
endmodule

module RegisterFile (
  input  WriteEnable,
  input  [4:0] WriteRegister,
  input  [31:0] WriteData,
  input  [4:0] ReadRegister1,
  input  [4:0] ReadRegister2,
  input  CLK,
  output [31:0] ReadData1,
  output [31:0] ReadData2
);

  wire and_1_out, and_2_out, and_3_out, and_4_out, and_5_out, and_6_out, and_7_out, and_8_out, and_9_out,
       and_10_out, and_11_out, and_12_out, and_13_out, and_14_out, and_15_out, and_16_out, and_17_out,
       and_18_out, and_19_out, and_20_out, and_21_out, and_22_out, and_23_out, and_24_out, and_25_out,
       and_26_out, and_27_out, and_28_out, and_29_out, and_30_out, and_31_out, and_32_out, decoder_1_out0,
       decoder_1_out1, decoder_1_out2, decoder_1_out3, decoder_1_out4, decoder_1_out5, decoder_1_out6,
       decoder_1_out7, decoder_1_out8, decoder_1_out9, decoder_1_out10, decoder_1_out11, decoder_1_out12,
       decoder_1_out13, decoder_1_out14, decoder_1_out15, decoder_1_out16, decoder_1_out17, decoder_1_out18,
       decoder_1_out19, decoder_1_out20, decoder_1_out21, decoder_1_out22, decoder_1_out23, decoder_1_out24,
       decoder_1_out25, decoder_1_out26, decoder_1_out27, decoder_1_out28, decoder_1_out29, decoder_1_out30,
       decoder_1_out31;
  wire [31:0] r0_q, r1_q, r2_q, r3_q, r4_q, r5_q, r6_q, r7_q, r8_q, r9_q, r10_q, r11_q, r12_q, r13_q, r14_q,
       r15_q, r16_q, r17_q, r18_q, r19_q, r20_q, r21_q, r22_q, r23_q, r24_q, r25_q, r26_q, r27_q, r28_q,
       r29_q, r30_q, r31_q;

  Decoder #(.select(5)) decoder_1 (
    .out0(decoder_1_out0), .out1(decoder_1_out1), .out2(decoder_1_out2), .out3(decoder_1_out3),
    .out4(decoder_1_out4), .out5(decoder_1_out5), .out6(decoder_1_out6), .out7(decoder_1_out7),
    .out8(decoder_1_out8), .out9(decoder_1_out9), .out10(decoder_1_out10), .out11(decoder_1_out11),
    .out12(decoder_1_out12), .out13(decoder_1_out13), .out14(decoder_1_out14), .out15(decoder_1_out15),
    .out16(decoder_1_out16), .out17(decoder_1_out17), .out18(decoder_1_out18), .out19(decoder_1_out19),
    .out20(decoder_1_out20), .out21(decoder_1_out21), .out22(decoder_1_out22), .out23(decoder_1_out23),
    .out24(decoder_1_out24), .out25(decoder_1_out25), .out26(decoder_1_out26), .out27(decoder_1_out27),
    .out28(decoder_1_out28), .out29(decoder_1_out29), .out30(decoder_1_out30), .out31(decoder_1_out31),
    .sel(WriteRegister));  // open: en
  and and_1 (and_1_out, decoder_1_out0, WriteEnable);
  and and_2 (and_2_out, decoder_1_out1, WriteEnable);
  and and_3 (and_3_out, decoder_1_out2, WriteEnable);
  and and_4 (and_4_out, decoder_1_out3, WriteEnable);
  and and_5 (and_5_out, decoder_1_out4, WriteEnable);
  and and_6 (and_6_out, decoder_1_out5, WriteEnable);
  and and_7 (and_7_out, decoder_1_out6, WriteEnable);
  and and_8 (and_8_out, decoder_1_out7, WriteEnable);
  and and_9 (and_9_out, decoder_1_out8, WriteEnable);
  and and_10 (and_10_out, decoder_1_out9, WriteEnable);
  and and_11 (and_11_out, decoder_1_out10, WriteEnable);
  and and_12 (and_12_out, decoder_1_out11, WriteEnable);
  and and_13 (and_13_out, decoder_1_out12, WriteEnable);
  and and_14 (and_14_out, decoder_1_out13, WriteEnable);
  and and_15 (and_15_out, decoder_1_out14, WriteEnable);
  and and_16 (and_16_out, decoder_1_out15, WriteEnable);
  and and_17 (and_17_out, decoder_1_out16, WriteEnable);
  and and_18 (and_18_out, decoder_1_out17, WriteEnable);
  and and_19 (and_19_out, decoder_1_out18, WriteEnable);
  and and_20 (and_20_out, decoder_1_out19, WriteEnable);
  and and_21 (and_21_out, decoder_1_out20, WriteEnable);
  and and_22 (and_22_out, decoder_1_out21, WriteEnable);
  and and_23 (and_23_out, decoder_1_out22, WriteEnable);
  and and_24 (and_24_out, decoder_1_out23, WriteEnable);
  and and_25 (and_25_out, decoder_1_out24, WriteEnable);
  and and_26 (and_26_out, decoder_1_out25, WriteEnable);
  and and_27 (and_27_out, decoder_1_out26, WriteEnable);
  and and_28 (and_28_out, decoder_1_out27, WriteEnable);
  and and_29 (and_29_out, decoder_1_out28, WriteEnable);
  and and_30 (and_30_out, decoder_1_out29, WriteEnable);
  and and_31 (and_31_out, decoder_1_out30, WriteEnable);
  and and_32 (and_32_out, decoder_1_out31, WriteEnable);
  Register #(.width(32)) r0 (.D(WriteData), .en(and_1_out), .clk(CLK), .Q(r0_q));  // open: clr
  Register #(.width(32)) r1 (.D(WriteData), .en(and_2_out), .clk(CLK), .Q(r1_q));  // open: clr
  Register #(.width(32)) r2 (.D(WriteData), .en(and_3_out), .clk(CLK), .Q(r2_q));  // open: clr
  Register #(.width(32)) r3 (.D(WriteData), .en(and_4_out), .clk(CLK), .Q(r3_q));  // open: clr
  Register #(.width(32)) r4 (.D(WriteData), .en(and_5_out), .clk(CLK), .Q(r4_q));  // open: clr
  Register #(.width(32)) r5 (.D(WriteData), .en(and_6_out), .clk(CLK), .Q(r5_q));  // open: clr
  Register #(.width(32)) r6 (.D(WriteData), .en(and_7_out), .clk(CLK), .Q(r6_q));  // open: clr
  Register #(.width(32)) r7 (.D(WriteData), .en(and_8_out), .clk(CLK), .Q(r7_q));  // open: clr
  Register #(.width(32)) r8 (.D(WriteData), .en(and_9_out), .clk(CLK), .Q(r8_q));  // open: clr
  Register #(.width(32)) r9 (.D(WriteData), .en(and_10_out), .clk(CLK), .Q(r9_q));  // open: clr
  Register #(.width(32)) r10 (.D(WriteData), .en(and_11_out), .clk(CLK), .Q(r10_q));  // open: clr
  Register #(.width(32)) r11 (.D(WriteData), .en(and_12_out), .clk(CLK), .Q(r11_q));  // open: clr
  Register #(.width(32)) r12 (.D(WriteData), .en(and_13_out), .clk(CLK), .Q(r12_q));  // open: clr
  Register #(.width(32)) r13 (.D(WriteData), .en(and_14_out), .clk(CLK), .Q(r13_q));  // open: clr
  Register #(.width(32)) r14 (.D(WriteData), .en(and_15_out), .clk(CLK), .Q(r14_q));  // open: clr
  Register #(.width(32)) r15 (.D(WriteData), .en(and_16_out), .clk(CLK), .Q(r15_q));  // open: clr
  Register #(.width(32)) r16 (.D(WriteData), .en(and_17_out), .clk(CLK), .Q(r16_q));  // open: clr
  Register #(.width(32)) r17 (.D(WriteData), .en(and_18_out), .clk(CLK), .Q(r17_q));  // open: clr
  Register #(.width(32)) r18 (.D(WriteData), .en(and_19_out), .clk(CLK), .Q(r18_q));  // open: clr
  Register #(.width(32)) r19 (.D(WriteData), .en(and_20_out), .clk(CLK), .Q(r19_q));  // open: clr
  Register #(.width(32)) r20 (.D(WriteData), .en(and_21_out), .clk(CLK), .Q(r20_q));  // open: clr
  Register #(.width(32)) r21 (.D(WriteData), .en(and_22_out), .clk(CLK), .Q(r21_q));  // open: clr
  Register #(.width(32)) r22 (.D(WriteData), .en(and_23_out), .clk(CLK), .Q(r22_q));  // open: clr
  Register #(.width(32)) r23 (.D(WriteData), .en(and_24_out), .clk(CLK), .Q(r23_q));  // open: clr
  Register #(.width(32)) r24 (.D(WriteData), .en(and_25_out), .clk(CLK), .Q(r24_q));  // open: clr
  Register #(.width(32)) r25 (.D(WriteData), .en(and_26_out), .clk(CLK), .Q(r25_q));  // open: clr
  Register #(.width(32)) r26 (.D(WriteData), .en(and_27_out), .clk(CLK), .Q(r26_q));  // open: clr
  Register #(.width(32)) r27 (.D(WriteData), .en(and_28_out), .clk(CLK), .Q(r27_q));  // open: clr
  Register #(.width(32)) r28 (.D(WriteData), .en(and_29_out), .clk(CLK), .Q(r28_q));  // open: clr
  Register #(.width(32)) r29 (.D(WriteData), .en(and_30_out), .clk(CLK), .Q(r29_q));  // open: clr
  Register #(.width(32)) r30 (.D(WriteData), .en(and_31_out), .clk(CLK), .Q(r30_q));  // open: clr
  Register #(.width(32)) r31 (.D(WriteData), .en(and_32_out), .clk(CLK), .Q(r31_q));  // open: clr
  Multiplexer #(.enable("false"), .select(5), .width(32)) multiplexer_1 (
    .in0(r0_q), .in1(r1_q), .in2(r2_q), .in3(r3_q), .in4(r4_q), .in5(r5_q), .in6(r6_q), .in7(r7_q),
    .in8(r8_q), .in9(r9_q), .in10(r10_q), .in11(r11_q), .in12(r12_q), .in13(r13_q), .in14(r14_q),
    .in15(r15_q), .in16(r16_q), .in17(r17_q), .in18(r18_q), .in19(r19_q), .in20(r20_q), .in21(r21_q),
    .in22(r22_q), .in23(r23_q), .in24(r24_q), .in25(r25_q), .in26(r26_q), .in27(r27_q), .in28(r28_q),
    .in29(r29_q), .in30(r30_q), .in31(r31_q), .out(ReadData1), .sel(ReadRegister1));
  Multiplexer #(.enable("false"), .select(5), .width(32)) multiplexer_2 (
    .in0(r0_q), .in1(r1_q), .in2(r2_q), .in3(r3_q), .in4(r4_q), .in5(r5_q), .in6(r6_q), .in7(r7_q),
    .in8(r8_q), .in9(r9_q), .in10(r10_q), .in11(r11_q), .in12(r12_q), .in13(r13_q), .in14(r14_q),
    .in15(r15_q), .in16(r16_q), .in17(r17_q), .in18(r18_q), .in19(r19_q), .in20(r20_q), .in21(r21_q),
    .in22(r22_q), .in23(r23_q), .in24(r24_q), .in25(r25_q), .in26(r26_q), .in27(r27_q), .in28(r28_q),
    .in29(r29_q), .in30(r30_q), .in31(r31_q), .out(ReadData2), .sel(ReadRegister2));
endmodule

module Memory (
  input  [31:0] MemAddr,
  input  MemWrite,
  input  [31:0] MemWriteData,
  input  MemRead,
  input  CLK,
  output [31:0] MemData
);

  wire [31:0] ram_1_dout;

  RAM #(.addrWidth(24), .dataWidth(32), .enables("line"), .\type ("nonvolatile")) ram_1 (
    .addr(MemAddr[25:2]), .we(MemWrite), .clk(CLK), .din(MemWriteData), .dout(ram_1_dout));
  Register #(.trigger("high"), .width(32)) register_1 (
    .D(ram_1_dout), .en(MemRead), .clk(MemRead), .Q(MemData));  // open: clr
endmodule

module SignExtend (
  input  [15:0] In16,
  output [31:0] Out32
);


  assign Out32 = {{17{In16[15]}}, In16[14:0]};
endmodule

module ShiftL2_32bit (
  input  [31:0] In32,
  output [31:0] OutShift32
);

  Shifter #(.width(32)) shifter_1 (.in(In32), .\dist (5'b00010), .out(OutShift32));
endmodule

module ShiftLeft26BitTo28 (
  input  [25:0] In26,
  output [27:0] Out28
);


  assign Out28 = {In26, 2'b00};
endmodule

module ControlUnit (
  input  [5:0] Op,
  input  Overflow,
  input  CLK,
  output PCWriteCond,
  output PCWrite,
  output IorD,
  output MemRead,
  output MemWrite,
  output MemtoReg,
  output IRWrite,
  output CauseWrite,
  output IntCause,
  output EPCWrite,
  output [1:0] PCSource,
  output [1:0] ALUOp,
  output [1:0] ALUSrcA,
  output [1:0] ALUSrcB,
  output RegWrite,
  output RegDst,
  output ReadSrc
);

  wire [3:0] CurrentState_q, nextstatecontrolunit_1_nextstate;

  NextStateControlUnit nextstatecontrolunit_1 (
    .CurrentState(CurrentState_q), .Op(Op), .Overflow(Overflow), .NextState(nextstatecontrolunit_1_nextstate));
  Register #(.width(4)) CurrentState (
    .D(nextstatecontrolunit_1_nextstate), .en(1'b1), .clk(CLK), .Q(CurrentState_q));  // open: clr
  OutputControlUnit outputcontrolunit_1 (
    .CurrentState(CurrentState_q), .PCWriteCond(PCWriteCond), .PCWrite(PCWrite), .IorD(IorD),
    .MemRead(MemRead), .MemWrite(MemWrite), .MemtoReg(MemtoReg), .IRWrite(IRWrite), .CauseWrite(CauseWrite),
    .IntCause(IntCause), .EPCWrite(EPCWrite), .PCSource(PCSource), .ALUOp(ALUOp), .ALUSrcA(ALUSrcA),
    .ALUSrcB(ALUSrcB), .RegWrite(RegWrite), .RegDst(RegDst), .ReadSrc(ReadSrc));
endmodule

module OverflowDetect (
  input  SignA,
  input  SignB,
  input  SignOut,
  output Overflow
);

  wire and_1_out, and_2_out, not_1_out, not_2_out, not_3_out;

  not not_1 (not_1_out, SignA);
  not not_2 (not_2_out, SignB);
  not not_3 (not_3_out, SignOut);
  and and_1 (and_1_out, not_1_out, not_2_out, SignOut);
  and and_2 (and_2_out, SignA, SignB, not_3_out);
  or or_1 (Overflow, and_1_out, and_2_out);
endmodule

module NextStateControlUnit (
  input  [3:0] CurrentState,
  input  [5:0] Op,
  input  Overflow,
  output [3:0] NextState
);

  wire and_1_out, and_2_out, and_3_out, and_4_out, and_5_out, and_6_out, and_7_out, and_8_out, and_9_out,
       and_10_out, and_11_out, and_12_out, and_13_out, and_14_out, and_15_out, and_16_out, and_17_out,
       and_18_out, and_19_out, and_20_out, and_21_out, and_22_out, and_23_out, and_24_out, and_25_out,
       and_26_out, and_27_out, and_28_out, and_29_out, and_30_out, and_31_out, and_32_out, not_1_out,
       not_2_out, not_3_out, not_4_out, not_5_out, not_6_out, not_7_out, not_8_out, not_9_out, not_10_out;

  not not_1 (not_1_out, CurrentState[3]);
  not not_2 (not_2_out, CurrentState[2]);
  not not_3 (not_3_out, CurrentState[1]);
  not not_4 (not_4_out, CurrentState[0]);
  not not_5 (not_5_out, Op[5]);
  not not_6 (not_6_out, Op[4]);
  not not_7 (not_7_out, Op[3]);
  not not_8 (not_8_out, Op[2]);
  not not_9 (not_9_out, Op[1]);
  not not_10 (not_10_out, Op[0]);
  and and_1 (and_1_out, not_1_out, not_2_out, not_3_out, CurrentState[0], not_9_out, Op[0]);
  and and_2 (and_2_out, not_1_out, not_2_out, not_3_out, CurrentState[0], not_5_out, Op[1]);
  and and_3 (and_3_out, not_1_out, not_2_out, not_3_out, CurrentState[0], Op[1], not_10_out);
  and and_4 (and_4_out, not_1_out, not_2_out, not_3_out, CurrentState[0], Op[2]);
  and and_5 (and_5_out, not_1_out, not_2_out, not_3_out, CurrentState[0], Op[3], not_9_out);
  and and_6 (and_6_out, not_1_out, not_2_out, not_3_out, CurrentState[0], Op[4]);
  and and_7 (and_7_out, not_1_out, not_2_out, not_3_out, CurrentState[0], Op[5], not_9_out);
  and and_8 (and_8_out, CurrentState[2], CurrentState[1], CurrentState[0], Overflow);
  and and_9 (and_9_out, CurrentState[3], CurrentState[2], not_4_out);
  and and_10 (and_10_out, not_1_out, not_2_out, CurrentState[0], not_5_out, not_6_out, not_7_out, not_8_out, not_9_out, not_10_out);
  and and_11 (and_11_out, not_1_out, not_2_out, CurrentState[0], not_5_out, not_6_out, Op[3], not_8_out, not_9_out, Op[0]);
  and and_12 (and_12_out, not_1_out, CurrentState[1], not_4_out, Op[3]);
  and and_13 (and_13_out, not_1_out, not_2_out, CurrentState[1], CurrentState[0]);
  and and_14 (and_14_out, CurrentState[2], CurrentState[1], not_4_out);
  and and_15 (and_15_out, CurrentState[3], CurrentState[2]);
  and and_16 (and_16_out, not_1_out, not_2_out, not_3_out, CurrentState[0], not_7_out, not_8_out, not_9_out);
  and and_17 (and_17_out, not_1_out, not_2_out, not_3_out, CurrentState[0], not_7_out, Op[0]);
  and and_18 (and_18_out, not_1_out, not_2_out, not_3_out, CurrentState[0], Op[2], Op[0]);
  and and_19 (and_19_out, not_1_out, not_2_out, not_3_out, CurrentState[0], Op[2], Op[1]);
  and and_20 (and_20_out, not_1_out, not_2_out, not_3_out, CurrentState[0], Op[3], not_10_out);
  and and_21 (and_21_out, not_1_out, not_2_out, not_3_out, CurrentState[0], Op[3], Op[1]);
  and and_22 (and_22_out, not_1_out, not_2_out, not_3_out, CurrentState[0], Op[4]);
  and and_23 (and_23_out, not_1_out, not_2_out, not_3_out, CurrentState[0], Op[5]);
  and and_24 (and_24_out, not_1_out, CurrentState[1], not_4_out, not_7_out);
  and and_25 (and_25_out, CurrentState[2], CurrentState[1], not_4_out);
  and and_26 (and_26_out, CurrentState[2], CurrentState[1], Overflow);
  and and_27 (and_27_out, CurrentState[3], CurrentState[2], CurrentState[0]);
  and and_28 (and_28_out, not_1_out, not_2_out, not_4_out);
  and and_29 (and_29_out, not_1_out, not_2_out, not_3_out, not_5_out, not_6_out, not_7_out, not_8_out, Op[1], not_10_out);
  and and_30 (and_30_out, not_1_out, CurrentState[1], not_4_out);
  and and_31 (and_31_out, CurrentState[2], CurrentState[1], Overflow);
  and and_32 (and_32_out, CurrentState[3], CurrentState[2]);
  or or_1 (NextState[3], and_1_out, and_2_out, and_3_out, and_4_out, and_5_out, and_6_out, and_7_out, and_8_out, and_9_out);
  or or_2 (NextState[2], and_10_out, and_11_out, and_12_out, and_13_out, and_14_out, and_15_out);
  or or_3 (NextState[0], and_28_out, and_29_out, and_30_out, and_31_out, and_32_out);
  or or_4 (NextState[1], and_16_out, and_17_out, and_18_out, and_19_out, and_20_out, and_21_out, and_22_out, and_23_out, and_24_out, and_25_out, and_26_out, and_27_out);
endmodule

module OutputControlUnit (
  input  [3:0] CurrentState,
  output PCWriteCond,
  output PCWrite,
  output IorD,
  output MemRead,
  output MemWrite,
  output MemtoReg,
  output IRWrite,
  output CauseWrite,
  output IntCause,
  output EPCWrite,
  output [1:0] PCSource,
  output [1:0] ALUOp,
  output [1:0] ALUSrcA,
  output [1:0] ALUSrcB,
  output RegWrite,
  output RegDst,
  output ReadSrc
);

  wire and_2_out, and_3_out, and_4_out, and_5_out, and_6_out, and_7_out, and_8_out, and_15_out, and_16_out,
       and_17_out, and_18_out, and_20_out, and_21_out, and_23_out, and_24_out, and_25_out, and_26_out,
       and_27_out, and_28_out, and_29_out, and_30_out, not_1_out, not_2_out, not_3_out, not_4_out;

  not not_1 (not_1_out, CurrentState[3]);
  not not_2 (not_2_out, CurrentState[2]);
  not not_3 (not_3_out, CurrentState[1]);
  not not_4 (not_4_out, CurrentState[0]);
  and and_1 (PCWriteCond, CurrentState[3], not_2_out, not_3_out, not_4_out);
  and and_2 (and_2_out, not_1_out, not_2_out, not_3_out, not_4_out);
  and and_3 (and_3_out, CurrentState[3], not_2_out, CurrentState[0]);
  and and_4 (and_4_out, CurrentState[3], CurrentState[1]);
  and and_5 (and_5_out, not_1_out, not_2_out, CurrentState[1], CurrentState[0]);
  and and_6 (and_6_out, not_1_out, CurrentState[2], not_3_out, CurrentState[0]);
  and and_7 (and_7_out, not_1_out, not_2_out, not_3_out, not_4_out);
  and and_8 (and_8_out, not_1_out, not_2_out, CurrentState[1], CurrentState[0]);
  and and_9 (MemWrite, not_1_out, CurrentState[2], not_3_out, CurrentState[0]);
  and and_10 (MemtoReg, not_1_out, CurrentState[2], not_3_out, not_4_out);
  and and_11 (IRWrite, not_1_out, not_2_out, not_3_out, not_4_out);
  and and_12 (CauseWrite, CurrentState[3], CurrentState[1]);
  and and_13 (IntCause, CurrentState[3], CurrentState[1], CurrentState[0]);
  and and_14 (EPCWrite, CurrentState[3], CurrentState[1]);
  and and_15 (and_15_out, CurrentState[3], not_2_out, CurrentState[0]);
  and and_16 (and_16_out, CurrentState[3], CurrentState[1]);
  and and_17 (and_17_out, CurrentState[3], not_2_out, not_4_out);
  and and_18 (and_18_out, CurrentState[3], CurrentState[1]);
  and and_19 (ALUOp[1], CurrentState[2], CurrentState[1], not_4_out);
  and and_20 (and_20_out, CurrentState[3], not_2_out, not_4_out);
  and and_21 (and_21_out, CurrentState[3], CurrentState[1]);
  and and_22 (ALUSrcA[1], CurrentState[3], CurrentState[2], CurrentState[0]);
  and and_23 (and_23_out, not_1_out, CurrentState[1], not_4_out);
  and and_24 (and_24_out, CurrentState[3], not_3_out, not_4_out);
  and and_25 (and_25_out, not_1_out, not_2_out, not_3_out, CurrentState[0]);
  and and_26 (and_26_out, not_1_out, not_2_out, CurrentState[1], not_4_out);
  and and_27 (and_27_out, not_1_out, not_2_out, not_3_out);
  and and_28 (and_28_out, CurrentState[3], CurrentState[1]);
  and and_29 (and_29_out, not_1_out, CurrentState[2], not_3_out, not_4_out);
  and and_30 (and_30_out, CurrentState[2], CurrentState[1], CurrentState[0]);
  and and_31 (RegDst, CurrentState[2], CurrentState[1], CurrentState[0]);
  and and_32 (ReadSrc, CurrentState[3], CurrentState[2], not_4_out);
  or or_1 (PCWrite, and_2_out, and_3_out, and_4_out);
  or or_2 (IorD, and_5_out, and_6_out);
  or or_3 (MemRead, and_7_out, and_8_out);
  or or_4 (PCSource[1], and_15_out, and_16_out);
  or or_5 (PCSource[0], and_17_out, and_18_out);
  or or_6 (ALUOp[0], and_20_out, and_21_out);
  or or_7 (ALUSrcA[0], and_23_out, and_24_out);
  or or_8 (ALUSrcB[1], and_25_out, and_26_out);
  or or_9 (ALUSrcB[0], and_27_out, and_28_out);
  or or_10 (RegWrite, and_29_out, and_30_out);
endmodule
